// Logisim project MATRIX.circ as structural Verilog: 1 circuit, main circuit MAC
module MAC (
  input  [31:0] A,
  input  [31:0] X,
  input  [31:0] B,
  input  clock,
  output [31:0] Result,
  output Done
);

  wire customadder_1_p1, customadder_2_p1, customadder_3_p1, customadder_4_p1;

  // CustomAdder customadder_1: pin names not known; wires that end beside it: customadder_1_p1, customadder_1_p1
  // CustomAdder customadder_2: pin names not known; wires that end beside it: customadder_2_p1, customadder_2_p1, B[15:8], B[7:0]
  // CustomAdder customadder_3: pin names not known; wires that end beside it: customadder_3_p1, customadder_3_p1, B[23:16]
  // CustomAdder customadder_4: pin names not known; wires that end beside it: customadder_4_p1, B[31:24], customadder_4_p1
  // CustomAdder customadder_5: pin names not known; wires that end beside it: Result[15:8]
  // CustomAdder customadder_6: pin names not known; wires that end beside it: Result[31:24]
  // CustomAdder customadder_7: pin names not known; wires that end beside it: Result[7:0]
  // CustomAdder customadder_8: pin names not known; wires that end beside it: Result[23:16]

  // Other names for the same wires on the sheet: A_1_1[7:0] = A[7:0]; A_1_2[7:0] = A[15:8]; A_2_1[7:0] = A[23:16];
  //   A_2_2[7:0] = A[31:24]; B_1_1[7:0] = B[7:0]; B_1_2[7:0] = B[15:8]; B_2_1[7:0] = B[23:16]; B_2_2[7:0] = B[31:24];
  //   clk = clock; Result_1_1[7:0] = Result[7:0]; Result_1_2[7:0] = Result[15:8]; Result_2_1[7:0] = Result[23:16];
  //   Result_2_2[7:0] = Result[31:24]; X_1_1[7:0] = X[7:0]; X_1_2[7:0] = X[15:8]; X_2_1[7:0] = X[23:16];
  //   X_2_2[7:0] = X[31:24]

  // Notes on the sheet:
  //   Please don't change places of inputs and outputs
endmodule
